# Fritzing sketch Photon Wiring (saved by Fritzing 0.9.3b)

parts:
  Bauteil2 = Photon
  R2 = Resistor [tolerance=±5% resistance=1k package=THT]
  U2 = 2-Channel 5v Relay Shield [package=relay-2ch5v10a]
  RHT2 = Humidity and Temperature Sensor RHT03
  J2 = shrouded pin header, 10 pins [form="♂ (shrouded male)"]

nets:
  N1: Bauteil2.RX, J2.pin3
  N2: Bauteil2.TX, J2.pin9
  GND: Bauteil2.GND, U2.GND, RHT2.GND_2, J2.pin1
  VIN: Bauteil2.VIN, U2.VCC
  N3: Bauteil2.D0, U2.IN2
  N4: Bauteil2.D1, U2.IN1
  N5: Bauteil2.D2, R2.Pin_0, RHT2.Data-signal
  3V3: Bauteil2.3V3, R2.Pin_1, RHT2.Vcc

notes:
  [display on top, wheel on right]
  display on top, wheel on right
  Honeywell HR-20 serial-test interface

custom parts:
  2-Channel 5v Relay Shield: 2 Channel 5v Relay Shield w. 2x SPD-06VDC-SD-C
